// Logisim project TASK3_23K0078.circ as structural Verilog: 1 circuit, main circuit main
module main (
  input  in_1,
  input  in_2
);

  wire and_1_out, and_2_out, and_3_out, and_4_out, and_5_out, and_6_out, and_7_out, and_8_out, and_9_out,
       and_10_out, clock_1_out, clock_2_out, d_ff_1_q, d_ff_2_q, d_ff_3_q, d_ff_4_q, d_ff_5_q, d_ff_6_q,
       j_k_ff_1_q, j_k_ff_1_qn, j_k_ff_2_q, j_k_ff_2_qn, j_k_ff_3_q, j_k_ff_3_qn, j_k_ff_4_q, j_k_ff_4_qn,
       j_k_ff_5_q, j_k_ff_5_qn, j_k_ff_6_q, j_k_ff_6_qn, not_1_out, or_1_out, or_2_out, or_3_out, or_4_out,
       or_5_out;

  Clock clock_1 (.out(clock_1_out));
  Clock clock_2 (.out(clock_2_out));
  LED led_1 (.in(j_k_ff_1_q));
  J_K_Flip_Flop j_k_ff_1 (
    .J(in_1), .clk(clock_2_out), .K(in_1), .Q(j_k_ff_1_q), .Qn(j_k_ff_1_qn));  // open: preset, en, reset
  not not_1 (not_1_out, in_2);
  D_Flip_Flop d_ff_1 (.clk(clock_1_out), .D(j_k_ff_1_q), .Q(d_ff_1_q));  // open: Qn, preset, en, reset
  and and_1 (and_1_out, in_2, j_k_ff_1_q);
  and and_2 (and_2_out, j_k_ff_1_qn, not_1_out);
  LED led_2 (.in(d_ff_1_q));
  or or_1 (or_1_out, and_1_out, and_2_out);
  J_K_Flip_Flop j_k_ff_2 (
    .J(or_1_out), .clk(clock_2_out), .K(or_1_out), .Q(j_k_ff_2_q), .Qn(j_k_ff_2_qn));  // open: preset, en, reset
  LED led_3 (.in(j_k_ff_2_q));
  and and_3 (and_3_out, and_1_out, j_k_ff_2_q);
  and and_4 (and_4_out, j_k_ff_2_qn, and_2_out);
  LED led_4 (.in(d_ff_2_q));
  D_Flip_Flop d_ff_2 (.clk(clock_1_out), .D(j_k_ff_2_q), .Q(d_ff_2_q));  // open: Qn, preset, en, reset
  or or_2 (or_2_out, and_3_out, and_4_out);
  LED led_5 (.in(j_k_ff_3_q));
  J_K_Flip_Flop j_k_ff_3 (
    .J(or_2_out), .clk(clock_2_out), .K(or_2_out), .Q(j_k_ff_3_q), .Qn(j_k_ff_3_qn));  // open: preset, en, reset
  LED led_6 (.in(d_ff_3_q));
  D_Flip_Flop d_ff_3 (.clk(clock_1_out), .D(j_k_ff_3_q), .Q(d_ff_3_q));  // open: Qn, preset, en, reset
  and and_5 (and_5_out, and_3_out, j_k_ff_3_q);
  and and_6 (and_6_out, j_k_ff_3_qn, and_4_out);
  or or_3 (or_3_out, and_5_out, and_6_out);
  LED led_7 (.in(j_k_ff_4_q));
  J_K_Flip_Flop j_k_ff_4 (
    .J(or_3_out), .clk(clock_2_out), .K(or_3_out), .Q(j_k_ff_4_q), .Qn(j_k_ff_4_qn));  // open: preset, en, reset
  LED led_8 (.in(d_ff_4_q));
  D_Flip_Flop d_ff_4 (.clk(clock_1_out), .D(j_k_ff_4_q), .Q(d_ff_4_q));  // open: Qn, preset, en, reset
  and and_7 (and_7_out, and_5_out, j_k_ff_4_q);
  and and_8 (and_8_out, j_k_ff_4_qn, and_6_out);
  or or_4 (or_4_out, and_7_out, and_8_out);
  LED led_9 (.in(j_k_ff_5_q));
  J_K_Flip_Flop j_k_ff_5 (
    .J(or_4_out), .clk(clock_2_out), .K(or_4_out), .Q(j_k_ff_5_q), .Qn(j_k_ff_5_qn));  // open: preset, en, reset
  D_Flip_Flop d_ff_5 (.clk(clock_1_out), .D(j_k_ff_5_q), .Q(d_ff_5_q));  // open: Qn, preset, en, reset
  and and_9 (and_9_out, and_7_out, j_k_ff_5_q);
  and and_10 (and_10_out, j_k_ff_5_qn, and_8_out);
  LED led_10 (.in(d_ff_5_q));
  or or_5 (or_5_out, and_9_out, and_10_out);
  J_K_Flip_Flop j_k_ff_6 (
    .J(or_5_out), .clk(clock_2_out), .K(or_5_out), .Q(j_k_ff_6_q), .Qn(j_k_ff_6_qn));  // open: preset, en, reset
  LED led_11 (.in(j_k_ff_6_q));
  D_Flip_Flop d_ff_6 (.clk(clock_1_out), .D(j_k_ff_6_q), .Q(d_ff_6_q));  // open: Qn, preset, en, reset
  LED led_12 (.in(d_ff_6_q));

  // Notes on the sheet:
  //   Shift/Load
endmodule
