// Logisim project TASK4_23K0078.circ as structural Verilog: 1 circuit, main circuit main
module main (
  input  CAR_A,
  input  CAR_B,
  input  CAR_C,
  input  CAR_D,
  input  in_5,
  input  PEDESTRIAN,
  input  [3:0] in_7,
  output [3:0] out_8
);

  wire and_1_out, and_2_out, and_3_out, clock_1_out, comparator_1_eq, not_1_out, not_2_out, not_3_out,
       not_4_out, not_5_out, or_1_out, or_2_out, or_3_out, or_4_out, or_5_out, or_6_out, or_7_out;
  wire [1:0] priority_encoder_1_out;
  wire [3:0] multiplexer_1_out;

  or or_1 (or_1_out, CAR_A, CAR_B);
  or or_2 (or_2_out, CAR_A, CAR_C);
  or or_3 (or_3_out, CAR_A, CAR_D);
  or or_4 (or_4_out, CAR_B, CAR_C);
  or or_5 (or_5_out, CAR_B, CAR_D);
  or or_6 (or_6_out, CAR_C, CAR_D);
  or or_7 (or_7_out, or_1_out, or_2_out, or_3_out, or_4_out, or_5_out, or_6_out);
  not not_1 (not_1_out, or_7_out);
  not not_2 (not_2_out, or_7_out);
  not not_3 (not_3_out, not_1_out);
  not not_4 (not_4_out, PEDESTRIAN);
  Priority_Encoder #(.select(2)) priority_encoder_1 (
    .in0(or_7_out), .in1(not_1_out), .in2(PEDESTRIAN), .out(priority_encoder_1_out));  // open: in3, gs, en_out, en_in
  Multiplexer #(.select(2), .width(4)) multiplexer_1 (
    .in0(4'b1010), .in1(4'b0010), .in2(4'b0100), .out(multiplexer_1_out), .sel(priority_encoder_1_out));  // open: in3
  Clock clock_1 (.out(clock_1_out));
  Counter #(.max('hf), .ongoal("stay"), .width(4)) counter_1 (
    .load(in_5), .up(1'b0), .clk(clock_1_out), .D(multiplexer_1_out), .Q(out_8));  // open: clr, count, carry
  Comparator #(.width(4)) comparator_1 (.a(out_8), .b(in_7), .eq(comparator_1_eq));  // open: gt, lt
  not not_5 (not_5_out, comparator_1_eq);
  and and_1 (and_1_out, or_7_out, not_3_out, not_4_out, not_5_out);
  LED led_1 (.in(and_1_out));
  and and_2 (and_2_out, not_2_out, not_1_out, not_4_out);
  LED led_2 (.in(and_2_out));
  and and_3 (and_3_out, PEDESTRIAN, not_2_out, not_1_out, not_5_out);
  LED led_3 (.in(and_3_out));

  // Notes on the sheet:
  //   NO CARS PRESENT
endmodule
